# Fritzing sketch Scheme (saved by Fritzing 0.9.10b)
breadboards: 1

parts:
  ESP32 = MH-ET LIVE ESP32 DEVKIT 38 pins
  R1 = Resistor [tolerance=±5% power=0.25 resistance=1k package=THT]
  2N2222A = NPN-Transistor [package="TO92 [THT]"]
  D1_1N4001 = Diode [package=diode-hv]
  Thermo_Couple_MAX31855 = Adafruit Thermocouple Amplifier MAX31855 [part_number="Adafruit #269"]
  Solid_State_Relay_Terminal = female pin header, 2 pins [form="♀ (female)"]

nets:
  3V3: ESP32.3V3, Thermo_Couple_MAX31855.VIN
  N1: ESP32.IO25, Thermo_Couple_MAX31855.DO
  N2: ESP32.IO26, Thermo_Couple_MAX31855.CS
  N3: ESP32.IO27, Thermo_Couple_MAX31855.CLK
  N4: ESP32.5V, D1_1N4001.C, Solid_State_Relay_Terminal.pin1
  GND: ESP32.GND#64, Thermo_Couple_MAX31855.GND
  N5: ESP32.IO23, R1.Pin_0
  N6: R1.Pin_1, 2N2222A.B
  N7: 2N2222A.C, D1_1N4001.A, Solid_State_Relay_Terminal.pin2

custom parts:
  MH-ET LIVE ESP32 DEVKIT 38 pins: http://mh.nodebb.com/topic/2/mh-et-live-esp32-devkit
  Adafruit Thermocouple Amplifier MAX31855: Thermocouples are very sensitive, requiring a good amplifier with a cold-compensation reference. The MAX31855K does everything for you, and can be easily interfaced with any microcontroller, even one without an analog input. This breakout board has the chip itself, a 3.3V regulator with 10uF bypass capacitors and level shifting circuitry, all assembled and tested. Comes with a 2 pin terminal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
